# Fritzing sketch IoT_lamp_12V_LED (saved by Fritzing 0.9.9b)

parts:
  BARREL_CONN = Power Jack [package=power_jack_smd]
  LED1 = LED - 3mm [color="Red (633nm)" current=0.030 package="3 mm [THT]"]
  WeMos_D1_Mini_Relay_Shield_V1 = WeMos D1 Mini Relay Shield V2
  HLK-PM1 = HLK-PM12 [part_number=HLK-PM12]
  BARREL_CONN1 = Power Jack [package=power_jack_smd]

nets:
  N1: BARREL_CONN.GND, LED1.cathode
  N2: BARREL_CONN.GNDBREAK, WeMos_D1_Mini_Relay_Shield_V1.NO
  N3: LED1.anode, WeMos_D1_Mini_Relay_Shield_V1.COM
  N4: HLK-PM1.-Vo, BARREL_CONN1.GND
  N5: HLK-PM1.+Vo, BARREL_CONN1.GNDBREAK
